# Fritzing sketch 微處理器期末實體接線圖 (saved by Fritzing 0.9.3b)
breadboards: 1

parts:
  R1 = Resistor [tolerance=±5% resistance=220 package=THT]
  M2 = LJ18A3-B-Z/BY [package=THT]
  R2 = Photocell (LDR) [package=THT]
  hc-sr1 = hc-sr04
  元件1 = Arduino Uno (Rev3) - ICSP
  J5 = Basic Servo
  J7 = Basic Servo
  R3 = Resistor [tolerance=±5% resistance=220 package=THT]
  R4 = Resistor [tolerance=±5% resistance=220 package=THT]
  R5 = Resistor [tolerance=±5% resistance=220 package=THT]
  VCC1 = Battery block 9V  # not connected

nets:
  VCC: R1.Pin_0, M2.VI_(BRN), 元件1.5V, J5.vcc, J7.vcc
  N1: R1.Pin_1, hc-sr1.VCC
  GND: M2.VO_(BLU), 元件1.GND, J5.gnd, J7.gnd, R3.Pin_0, R5.Pin_1
  N2: M2.SIG_(BLK), 元件1.D2
  N3: R2.pin_0, R4.Pin_0
  N4: R2.pin_1, 元件1.A0
  N5: hc-sr1.Trig, 元件1.ICSP_MISO, 元件1.D12/MISO
  N6: hc-sr1.Echo, 元件1.D13/SCK
  N7: hc-sr1.GND, R3.Pin_1
  N8: 元件1.D4, J7.pulse
  N9: 元件1.D6_PWM, J5.pulse

notes:
  servo 1
  servo 2

custom parts:
  LJ18A3-B-Z/BY: LJ18A3-B-Z/BX Proximity Sensor module.
